# Fritzing sketch Fotocelda (saved by Fritzing 0.8.7b)
breadboards: 1

parts:
  M1 = Arduino Nano (Rev3.0)
  F_R2 = Photocell (LDR) [package=THT]
  R1 = Resistor [tolerance=±5% resistance=10k package=THT]
  R2 = Resistor [tolerance=±5% resistance=220 package=THT]
  LED1 = LED - 5mm [color="Red (633nm)" package="5 mm [THT]"]

nets:
  N1: M1.D2, R2.Pin_0
  N2: M1.VIN, F_R2.pin_1
  N3: M1.GND, R1.Pin_0, LED1.cathode
  N4: M1.A1, F_R2.pin_0, R1.Pin_1
  N5: R2.Pin_1, LED1.anode
