# Fritzing sketch MotorDC (saved by Fritzing 0.8.7b)
breadboards: 1

parts:
  M1 = Arduino Nano (Rev3.0)
  Q1 = NPN-Transistor [package="TO92 [THT]"]
  R1 = Resistor [tolerance=±5% resistance=330 package=THT]
  LED1 = LED - 5mm [color="Red (633nm)" package="5 mm [THT]"]
  M1_2 = DC Motor

nets:
  N1: M1.GND, LED1.anode, M1_2.pin_1
  N2: M1.D2, R1.Pin_1
  N3: M1.5V, Q1.C
  N4: Q1.E, LED1.cathode, M1_2.pin_2
  N5: Q1.B, R1.Pin_0
