# Fritzing sketch Potenciometro (saved by Fritzing 0.8.7b)
breadboards: 1

parts:
  M1 = Arduino Nano (Rev3.0)
  LED1 = LED - 5mm [color="Red (633nm)" package="5 mm [THT]"]
  R1 = Resistor [tolerance=±5% resistance=220 package=THT]
  R2 = Rotary Potentiometer (Small) [maximum_resistance=100kΩ package=THT]

nets:
  N1: M1.D2, R1.Pin_1
  N2: M1.VIN, R2.leg1
  N3: M1.GND, LED1.cathode, R2.leg2
  N4: M1.A7, R2.wiper
  N5: LED1.anode, R1.Pin_0
