# Fritzing sketch Pulsador (saved by Fritzing 0.8.7b)
breadboards: 1

parts:
  M1 = Arduino Nano (Rev3.0)
  LED1 = LED - 5mm [color="Red (633nm)" package="5 mm [THT]"]
  R1 = Resistor [tolerance=±5% resistance=220 package=THT]
  R2 = Resistor [tolerance=±5% resistance=220 package=THT]
  S1 = Pushbutton [package=THT]

nets:
  N1: M1.D2, R1.Pin_1
  N2: M1.D3, R2.Pin_0, S1.leg0
  N3: M1.VIN, S1.leg1
  N4: M1.GND, LED1.cathode
  N5: LED1.anode, R1.Pin_0
