# Fritzing sketch RGB (saved by Fritzing 0.8.7b)
breadboards: 1

parts:
  M1 = Arduino Nano (Rev3.0)
  LED2 = RGB LED (com. anode, rbg) [package="5 mm [THT]"]
  R2 = Resistor [tolerance=±5% resistance=220 package=THT]
  R3 = Resistor [tolerance=±5% resistance=220 package=THT]
  R1 = Resistor [tolerance=±5% resistance=220 package=THT]

nets:
  N1: M1.GND, LED2.common_anode
  N2: M1.D2, R1.Pin_1
  N3: M1.D3, R2.Pin_1
  N4: M1.D4, R3.Pin_1
  N5: LED2.red_cathode, R1.Pin_0
  N6: LED2.blue_cathode, R2.Pin_0
  N7: LED2.green_cathode, R3.Pin_0
