# Fritzing sketch Semáforo (saved by Fritzing 0.8.7b)
breadboards: 1

parts:
  M1 = Arduino Nano (Rev3.0)
  R1 = Resistor [tolerance=±5% resistance=10k package=THT]
  S1 = Pushbutton [package=THT]
  LED6 = LED - 5mm [color="Green (555nm)" package="5 mm [THT]"]
  LED7 = LED - 5mm [color="Red (633nm)" package="5 mm [THT]"]
  LED8 = LED - 5mm [color="Green (555nm)" package="5 mm [THT]"]
  LED9 = LED - 5mm [color="Yellow (592nm)" package="5 mm [THT]"]
  LED10 = LED - 5mm [color="Red (633nm)" package="5 mm [THT]"]
  R2 = Resistor [tolerance=±5% resistance=220 package=THT]
  R3 = Resistor [tolerance=±5% resistance=220 package=THT]
  R4 = Resistor [tolerance=±5% resistance=220 package=THT]
  R5 = Resistor [tolerance=±5% resistance=220 package=THT]
  R6 = Resistor [tolerance=±5% resistance=220 package=THT]

nets:
  N1: M1.GND, R1.Pin_1, R2.Pin_1, R3.Pin_1, R4.Pin_1, R5.Pin_1, R6.Pin_1
  N2: M1.D3, R1.Pin_0, S1.leg0
  N3: M1.D4, LED10.anode
  N4: M1.D5, LED9.anode
  N5: M1.D6, LED8.anode
  N6: M1.D7, LED7.anode
  N7: M1.D8, LED6.anode
  N8: M1.VIN, S1.leg1
  N9: LED6.cathode, R6.Pin_0
  N10: LED7.cathode, R5.Pin_0
  N11: LED8.cathode, R4.Pin_0
  N12: LED9.cathode, R3.Pin_0
  N13: LED10.cathode, R2.Pin_0
