# Fritzing sketch Servomotor (saved by Fritzing 0.8.7b)
breadboards: 1

parts:
  M1 = Arduino Nano (Rev3.0)
  J1 = Basic Servo
  R1 = Rotary Potentiometer (Small) [maximum_resistance=100kΩ package=THT]

nets:
  N1: M1.D2, J1.pulse
  VIN: M1.VIN, J1.vcc, R1.leg1
  GND: M1.GND, J1.gnd, R1.leg2
  N2: M1.A7, R1.wiper
